# Fritzing sketch prototype-using-pro-mini (saved by Fritzing 0.9.1b)
breadboards: 1

parts:
  パーツ1 = Arduino Pro Mini v13
  IC1 = IC, SIP package, 13 pins [chip_label="SUNHAYATO CK35"]

nets:
  3.3V: パーツ1.VCC, IC1.pin6
  GND: パーツ1.GND, IC1.pin1, IC1.pin5, IC1.pin8
  N1: パーツ1.D13/SCK, IC1.pin7
  N2: パーツ1.D12/MISO, IC1.pin9
  N3: パーツ1.D11_PWM/MOSI, IC1.pin4
  N4: パーツ1.D10_PWM/SS, IC1.pin3
