# Fritzing sketch prototype-using-trinket (saved by Fritzing 0.9.1b)
breadboards: 1

parts:
  TRINKET1 = Trinket 3V
  IC2 = IC, SIP package, 13 pins [chip_label="SUNHAYATO CK35"]

nets:
  GND: TRINKET1.no_name_yet#2, IC2.pin1, IC2.pin5, IC2.pin8
  N1: TRINKET1.no_name_yet#4, IC2.pin3
  N2: TRINKET1.no_name_yet#6, IC2.pin6
  N3: TRINKET1.no_name_yet#7, IC2.pin7
  N4: TRINKET1.no_name_yet#8, IC2.pin4
  N5: TRINKET1.no_name_yet#9, IC2.pin9

custom parts:
  Trinket 3V: Adafruit Trinket 3V
